// Logisim project digit_controller.circ as structural Verilog: 2 circuits, main circuit main
module main (
);

  wire clock_1_out, clock_2_out, clock_3_out, clock_4_out, clock_5_out, clock_6_out, clock_7_out,
       clock_8_out, digit_controller_1_out_5, digit_controller_1_out_6, digit_controller_1_out_7,
       digit_controller_1_out_8, digit_controller_1_out_9, digit_controller_1_out_10,
       digit_controller_1_out_11, digit_controller_2_out_5, digit_controller_2_out_6,
       digit_controller_2_out_7, digit_controller_2_out_8, digit_controller_2_out_9,
       digit_controller_2_out_10, digit_controller_2_out_11;

  Clock #(.highDuration(8), .lowDuration(8)) clock_1 (.out(clock_1_out));
  Clock #(.highDuration(4), .lowDuration(4)) clock_2 (.out(clock_2_out));
  Clock #(.highDuration(4), .lowDuration(4)) clock_3 (.out(clock_3_out));
  Clock clock_4 (.out(clock_4_out));
  Clock #(.highDuration(2), .lowDuration(2)) clock_5 (.out(clock_5_out));
  Clock clock_6 (.out(clock_6_out));
  digit_controller digit_controller_1 (
    .D(clock_6_out), .C(clock_5_out), .B(clock_2_out), .A(clock_1_out), .out_5(digit_controller_1_out_5),
    .out_6(digit_controller_1_out_6), .out_7(digit_controller_1_out_7), .out_8(digit_controller_1_out_8),
    .out_9(digit_controller_1_out_9), .out_10(digit_controller_1_out_10), .out_11(digit_controller_1_out_11));
  Clock #(.highDuration(2), .lowDuration(2)) clock_7 (.out(clock_7_out));
  Clock #(.highDuration(8), .lowDuration(8)) clock_8 (.out(clock_8_out));
  digit_controller digit_controller_2 (
    .D(clock_8_out), .C(clock_7_out), .B(clock_3_out), .A(clock_4_out), .out_5(digit_controller_2_out_5),
    .out_6(digit_controller_2_out_6), .out_7(digit_controller_2_out_7), .out_8(digit_controller_2_out_8),
    .out_9(digit_controller_2_out_9), .out_10(digit_controller_2_out_10), .out_11(digit_controller_2_out_11));
  _7_Segment_Display u_7_segment_display_1 (
    .g(digit_controller_1_out_8), .f(digit_controller_1_out_7), .a(digit_controller_1_out_6),
    .b(digit_controller_1_out_5), .e(digit_controller_1_out_9), .d(digit_controller_1_out_10),
    .c(digit_controller_1_out_11));  // open: dp
  _7_Segment_Display u_7_segment_display_2 (
    .g(digit_controller_2_out_8), .f(digit_controller_2_out_7), .a(digit_controller_2_out_6),
    .b(digit_controller_2_out_5), .e(digit_controller_2_out_9), .d(digit_controller_2_out_10),
    .c(digit_controller_2_out_11));  // open: dp
endmodule

module digit_controller (
  input  D,
  input  C,
  input  B,
  input  A,
  output out_5,
  output out_6,
  output out_7,
  output out_8,
  output out_9,
  output out_10,
  output out_11
);

  wire and_1_out, and_2_out, and_3_out, and_4_out, and_5_out, and_6_out, and_7_out, and_8_out, and_9_out,
       and_10_out, and_11_out, and_12_out, and_13_out, and_14_out, and_15_out, and_16_out, and_17_out,
       and_18_out, and_19_out, and_20_out, and_21_out, and_22_out, and_23_out, and_24_out, and_25_out,
       and_26_out, and_27_out, nA_out, nB_out, nC_out, nD_out;

  not nD (nD_out, D);
  not nC (nC_out, C);
  not nB (nB_out, B);
  not nA (nA_out, A);
  and and_1 (and_1_out, nA_out, C, D);
  and and_2 (and_2_out, nB_out, nC_out);
  and and_3 (and_3_out, nA_out, nC_out, nD_out);
  and and_4 (and_4_out, nA_out, nB_out);
  or or_1 (out_5, and_3_out, and_4_out, and_2_out, and_1_out);
  and and_5 (and_5_out, A, nB_out, nC_out);
  and and_6 (and_6_out, nB_out, nC_out, nD_out);
  and and_7 (and_7_out, nA_out, C);
  and and_8 (and_8_out, nA_out, B, D);
  and and_9 (and_9_out, A, nB_out, nC_out);
  or or_2 (out_6, and_8_out, and_7_out, and_6_out, and_5_out);
  and and_10 (and_10_out, nA_out, nC_out, nD_out);
  and and_11 (and_11_out, nA_out, B, nD_out);
  and and_12 (and_12_out, nA_out, B, nC_out);
  or or_3 (out_7, and_11_out, and_12_out, and_10_out, and_9_out);
  and and_13 (and_13_out, A, nB_out, nC_out);
  and and_14 (and_14_out, nA_out, B, nC_out);
  and and_15 (and_15_out, nA_out, nB_out, C);
  and and_16 (and_16_out, nA_out, C, nD_out);
  and and_17 (and_17_out, nA_out, nB_out, nD_out);
  or or_4 (out_8, and_16_out, and_15_out, and_14_out, and_13_out);
  and and_18 (and_18_out, nA_out, C, nD_out);
  and and_19 (and_19_out, A, nB_out, nC_out, nD_out);
  or or_5 (out_9, and_19_out, and_18_out, and_17_out);
  and and_20 (and_20_out, nA_out, B, nC_out, D);
  and and_21 (and_21_out, A, nB_out, nC_out);
  and and_22 (and_22_out, nA_out, nB_out, C);
  and and_23 (and_23_out, nA_out, C, nD_out);
  and and_24 (and_24_out, nB_out, nC_out, nD_out);
  and and_25 (and_25_out, nB_out, nC_out);
  or or_6 (out_10, and_24_out, and_23_out, and_22_out, and_21_out, and_20_out);
  and and_26 (and_26_out, nA_out, D);
  and and_27 (and_27_out, nA_out, B);
  or or_7 (out_11, and_27_out, and_26_out, and_25_out);
endmodule
