// Logisim project reserver.circ as structural Verilog: 2 circuits, main circuit main
module main (
  input  \Профессор ,
  input  \Начальник_кафедры ,
  input  \Аспирант ,
  input  \Король_вечеринок 
);

  wire qwe_1_y0, qwe_1_y1, qwe_1_y2, qwe_1_y3;

  LED \u_Профессор  (.in(qwe_1_y0));
  qwe qwe_1 (
    .A0(\Профессор ), .A1(\Начальник_кафедры ), .A2(\Аспирант ), .A3(\Король_вечеринок ), .Y0(qwe_1_y0),
    .Y1(qwe_1_y1), .Y2(qwe_1_y2), .Y3(qwe_1_y3));
  LED \u_Начальник_Кафедры  (.in(qwe_1_y1));
  LED \u_Аспирант  (.in(qwe_1_y2));
  LED \u_Король_вечеринок  (.in(qwe_1_y3));
endmodule

module qwe (
  input  A0,
  input  A1,
  input  A2,
  input  A3,
  output Y0,
  output Y1,
  output Y2,
  output Y3
);

  and and_1 (Y1, ~A0, A1);  // AND_Gate
  and and_2 (Y2, ~A0, ~A1, A2);  // AND_Gate
  and and_3 (Y3, ~A0, ~A1, ~A2, A3);  // AND_Gate

  assign Y0 = A0;
endmodule
